# Fritzing sketch protoboard (saved by Fritzing 1.0.1rc)
perfboards: 1

parts:
  Pololu_A2 = Pololu A4988 [package=SO16]
  Mod2 = Amica NodeMCU DEVKIT 1.0
  S2 = H-Bridge with L298N
  M2 = Stepper Motor - Unipolar
  LimitClosed1 = Pushbutton [package=THT]
  LimitOpen1 = Pushbutton [package=THT]
  VacuumPresent1 = Pushbutton [package=THT]
  PSU2 = Adjustable Breadboard Power Supply
  JP1 = Header 4 [package=molex-1x4_lock]
  C2 = Electrolytic Capacitor [capacitance=100nF voltage=35V package="100 mil [THT, electrolytic]"]  # not connected

nets:
  N1: Pololu_A2.ENABLE, Mod2.pin_14
  N2: Pololu_A2.RESET, Pololu_A2.SLEEP
  N3: Pololu_A2.STEP, Mod2.pin_13
  N4: Pololu_A2.DIR, Mod2.pin_12
  GND: Pololu_A2.GND, Mod2.pin2, Mod2.pin_9, Mod2.pin_25, Mod2.pin_29, S2.GND, PSU2.Vin-
  N5: Pololu_A2.VDD, Mod2.pin1, Mod2.pin_10, Mod2.pin_26
  N6: Pololu_A2.1B, M2.D, JP1.4
  N7: Pololu_A2.1A, M2.B, JP1.3
  N8: Pololu_A2.2A, M2.C, JP1.2
  N9: Pololu_A2.2B, M2.A, JP1.1
  N10: Pololu_A2.VMOT, S2.12V, PSU2.Vin+
  N11: Mod2.pin6, LimitOpen1.leg1
  N12: Mod2.pin7, LimitClosed1.leg1
  N13: Mod2.pin8, VacuumPresent1.leg1
  N14: Mod2.pin_30, S2.5V

custom parts:
  H-Bridge with L298N: h-bridge
